// Logisim project COMPUTER rev1.circ as structural Verilog
module ALU (
  input  [15:0] A,
  input  [15:0] B,
  input  sel,
  output [15:0] out_4
);

  wire [15:0] adder_1_out, subtractor_1_out;

  Adder #(.width(16)) adder_1 (.a(A), .b(B), .out(adder_1_out));  // open: cin, cout
  Subtractor #(.width(16)) subtractor_1 (.a(A), .b(B), .out(subtractor_1_out));  // open: bin, bout
  Multiplexer #(.width(16), .enable("false")) multiplexer_1 (
    .in0(adder_1_out), .in1(subtractor_1_out), .out(out_4), .sel(sel));
endmodule

module CTRL_Unit (
  input  [15:0] Instr,
  input  reset,
  input  clk,
  output out_4,
  output DATA_ALU__AC,
  output AC_R_W,
  output AC_to_ALU_Out,
  output MBR_R_W,
  output MAR_R_W,
  output Data_Read,
  output Load,
  output Store,
  output Halt,
  output [11:0] Address
);

  wire [1:0] counter_1_q;
  wire [3:0] multiplexer_1_out;
  wire [9:9] rom_1_data;
  wire [11:0] PC_q;
  wire [15:0] counter_2_q;

  Counter #(.width(2), .max('h3)) counter_1 (.Q(counter_1_q), .clk(clk));  // open: load, D, count, carry, clr
  Counter #(.width(16), .max('hffff)) counter_2 (
    .D(Instr), .count(rom_1_data[9]), .Q(counter_2_q), .clk(counter_1_q[1]), .clr(reset));  // open: load, carry
  Multiplexer #(.width(4), .enable("false")) multiplexer_1 (
    .in0(4'b0000), .in1(counter_2_q[15:12]), .out(multiplexer_1_out), .sel(counter_1_q[1]));
  Counter #(.width(12), .max('hfff)) PC (.Q(PC_q), .clk(counter_1_q[1]), .clr(reset));  // open: load, D, count, carry
  Multiplexer #(.width(12), .enable("false")) multiplexer_2 (
    .in0(PC_q), .in1(counter_2_q[11:0]), .out(Address), .sel(counter_1_q[1]));
  ROM #(.addrWidth(4), .dataWidth(11)) rom_1 (
    .addr(multiplexer_1_out),
    .data({Halt, rom_1_data[9], Store, Load, Data_Read, MAR_R_W, MBR_R_W, AC_to_ALU_Out, AC_R_W, DATA_ALU__AC, out_4}));  // open: sel

  // Notes on the sheet:
  //   MSB/Opcode
  //   IR R/W
  //   contents of rom_1 (hex, n*v repeats v):
  //   6e0 4e4 528 402 403 5*0 400
endmodule

module CPU (
  input  [15:0] in_1,
  input  in_2,
  input  in_3,
  input  in_4,
  input  in_5,
  input  in_6,
  input  in_7,
  input  in_8,
  input  in_9,
  input  in_10,
  input  in_11,
  output [11:0] Address
);

  wire CLK_out;
  wire [15:0] AC_q, alu_1_out_4, controlled_buffer_1_out, demultiplexer_1_out0, demultiplexer_1_out1, MBR_q,
       multiplexer_1_out;

  Clock CLK (.out(CLK_out));
  assign controlled_buffer_1_out = in_8 ? in_1 : 16'bz;  // Controlled_Buffer controlled_buffer_1
  Register #(.width(12)) MAR (.en(in_7), .Q(Address), .clk(CLK_out));  // open: D, clr
  Register #(.width(16)) MBR (.D(controlled_buffer_1_out), .en(in_6), .Q(MBR_q), .clk(CLK_out));  // open: clr
  ALU alu_1 (.A(MBR_q), .B(demultiplexer_1_out1), .out_4(alu_1_out_4), .sel(in_2));
  Multiplexer #(.width(16), .enable("false")) multiplexer_1 (
    .in0(controlled_buffer_1_out), .in1(alu_1_out_4), .out(multiplexer_1_out), .sel(in_3));
  Register #(.width(16)) AC (.D(multiplexer_1_out), .en(in_4), .Q(AC_q), .clk(CLK_out));  // open: clr
  Demultiplexer #(.width(16), .enable("false")) demultiplexer_1 (
    .out0(demultiplexer_1_out0), .out1(demultiplexer_1_out1), .in(AC_q), .sel(in_5));
endmodule
