// Logisim project COMPUTER rev2.circ as structural Verilog
module ALU (
  input  [15:0] A,
  input  [15:0] B,
  input  sel,
  output [15:0] out_4
);

  wire [15:0] adder_1_out, subtractor_1_out;

  Adder #(.width(16)) adder_1 (.a(A), .b(B), .out(adder_1_out));  // open: cin, cout
  Subtractor #(.width(16)) subtractor_1 (.a(A), .b(B), .out(subtractor_1_out));  // open: bin, bout
  Multiplexer #(.width(16), .enable("false")) multiplexer_1 (
    .in0(adder_1_out), .in1(subtractor_1_out), .out(out_4), .sel(sel));
endmodule

module CTRL_Unit (
  input  [15:0] Instr,
  input  reset,
  input  clk,
  output out_4,
  output DATA_ALU__AC,
  output AC_R_W,
  output AC_to_ALU_Out,
  output MBR_R_W,
  output MAR_R_W,
  output Data_Read,
  output Load,
  output Store,
  output Halt,
  output [11:0] Address
);

  wire [1:0] counter_1_q;
  wire [3:0] multiplexer_1_out;
  wire [9:9] rom_1_data;
  wire [11:0] PC_q;
  wire [15:0] counter_2_q;

  Counter #(.width(2), .max('h3)) counter_1 (.Q(counter_1_q), .clk(clk));  // open: load, D, count, carry, clr
  Counter #(.width(16), .max('hffff)) counter_2 (
    .D(Instr), .count(rom_1_data[9]), .Q(counter_2_q), .clk(counter_1_q[1]), .clr(reset));  // open: load, carry
  Multiplexer #(.width(4), .enable("false")) multiplexer_1 (
    .in0(4'b0000), .in1(counter_2_q[15:12]), .out(multiplexer_1_out), .sel(counter_1_q[1]));
  Counter #(.width(12), .max('hfff)) PC (.Q(PC_q), .clk(counter_1_q[1]), .clr(reset));  // open: load, D, count, carry
  Multiplexer #(.width(12), .enable("false")) multiplexer_2 (
    .in0(PC_q), .in1(counter_2_q[11:0]), .out(Address), .sel(counter_1_q[1]));
  ROM #(.addrWidth(4), .dataWidth(11)) rom_1 (
    .addr(multiplexer_1_out),
    .data({Halt, rom_1_data[9], Store, Load, Data_Read, MAR_R_W, MBR_R_W, AC_to_ALU_Out, AC_R_W, DATA_ALU__AC, out_4}));  // open: sel

  // Notes on the sheet:
  //   MSB/Opcode
  //   IR R/W
  //   contents of rom_1 (hex, n*v repeats v):
  //   6e0 4e4 528 406 407 5*0 400
endmodule

module CPU (
  input  [15:0] in_1,
  input  reset,
  output [15:0] Data_Out,
  output [11:0] Address,
  output Load,
  output Store,
  output Halt
);

  wire CLK_out, ctrl_unit_1_ac_r_w, ctrl_unit_1_ac_to_alu_out, ctrl_unit_1_data_alu__ac,
       ctrl_unit_1_data_read, ctrl_unit_1_mar_r_w, ctrl_unit_1_mbr_r_w, ctrl_unit_1_out_4;
  wire [11:0] ctrl_unit_1_address;
  wire [15:0] AC_q, alu_1_out_4, controlled_buffer_1_out, demultiplexer_1_out0, MBR_q, multiplexer_1_out;

  Clock CLK (.out(CLK_out));
  CTRL_Unit ctrl_unit_1 (
    .Instr(controlled_buffer_1_out), .reset(reset), .out_4(ctrl_unit_1_out_4),
    .DATA_ALU__AC(ctrl_unit_1_data_alu__ac), .AC_R_W(ctrl_unit_1_ac_r_w),
    .AC_to_ALU_Out(ctrl_unit_1_ac_to_alu_out), .MBR_R_W(ctrl_unit_1_mbr_r_w), .MAR_R_W(ctrl_unit_1_mar_r_w),
    .Data_Read(ctrl_unit_1_data_read), .Load(Load), .Store(Store), .Halt(Halt),
    .Address(ctrl_unit_1_address), .clk(CLK_out));
  assign controlled_buffer_1_out = ctrl_unit_1_out_4 ? in_1 : 16'bz;  // Controlled_Buffer controlled_buffer_1
  Register #(.width(12)) MAR (
    .D(ctrl_unit_1_address), .en(ctrl_unit_1_data_read), .Q(Address), .clk(CLK_out));  // open: clr
  Register #(.width(16)) MBR (
    .D(controlled_buffer_1_out), .en(ctrl_unit_1_data_alu__ac), .Q(MBR_q), .clk(CLK_out));  // open: clr
  ALU alu_1 (.A(demultiplexer_1_out0), .B(MBR_q), .out_4(alu_1_out_4), .sel(ctrl_unit_1_mar_r_w));
  Multiplexer #(.width(16), .enable("false")) multiplexer_1 (
    .in0(controlled_buffer_1_out), .in1(alu_1_out_4), .out(multiplexer_1_out), .sel(ctrl_unit_1_ac_r_w));
  Demultiplexer #(.width(16), .enable("false")) demultiplexer_1 (
    .out0(demultiplexer_1_out0), .out1(Data_Out), .in(AC_q), .sel(ctrl_unit_1_mbr_r_w));
  Register #(.width(16)) AC (
    .D(multiplexer_1_out), .en(ctrl_unit_1_ac_to_alu_out), .Q(AC_q), .clk(CLK_out));  // open: clr
endmodule
