// Logisim project COMPUTER.circ as structural Verilog
module ALU (
  input  [15:0] A,
  input  [15:0] B,
  input  sel,
  output [15:0] out_4
);

  wire [15:0] adder_1_out, subtractor_1_out;

  Adder #(.width(16)) adder_1 (.a(A), .b(B), .out(adder_1_out));  // open: cin, cout
  Subtractor #(.width(16)) subtractor_1 (.a(A), .b(B), .out(subtractor_1_out));  // open: bin, bout
  Multiplexer #(.width(16), .enable("false")) multiplexer_1 (
    .in0(adder_1_out), .in1(subtractor_1_out), .out(out_4), .sel(sel));
endmodule

module CTRL_Unit (
  input  [15:0] Instr,
  input  reset,
  input  clk,
  output out_4,
  output out_5,
  output out_6,
  output out_7,
  output out_8,
  output out_9,
  output out_10,
  output out_11,
  output out_12,
  output out_13,
  output [11:0] Address
);

  wire [1:0] counter_1_q;
  wire [3:0] multiplexer_1_out;
  wire [9:9] rom_1_data;
  wire [11:0] PC_q;
  wire [15:0] counter_2_q;

  Counter #(.width(2), .max('h3)) counter_1 (.Q(counter_1_q), .clk(clk));  // open: load, D, count, carry, clr
  Counter #(.width(16), .max('hffff)) counter_2 (
    .D(Instr), .count(rom_1_data[9]), .Q(counter_2_q), .clk(counter_1_q[1]), .clr(reset));  // open: load, carry
  Multiplexer #(.width(4), .enable("false")) multiplexer_1 (
    .in0(4'b0000), .in1(counter_2_q[15:12]), .out(multiplexer_1_out), .sel(counter_1_q[1]));
  Counter #(.width(12), .max('hfff)) PC (.Q(PC_q), .clk(counter_1_q[1]), .clr(reset));  // open: load, D, count, carry
  Multiplexer #(.width(12), .enable("false")) multiplexer_2 (
    .in0(PC_q), .in1(counter_2_q[11:0]), .out(Address), .sel(counter_1_q[1]));
  ROM #(.addrWidth(4), .dataWidth(11)) rom_1 (
    .addr(multiplexer_1_out),
    .data({out_13, rom_1_data[9], out_12, out_11, out_10, out_9, out_8, out_7, out_6, out_5, out_4}));  // open: sel
endmodule

module CPU (
  output [11:0] Address
);

  wire CLK_out;
  wire [15:0] AC_q, alu_1_out_4, MBR_q, multiplexer_1_out;

  Clock CLK (.out(CLK_out));
  Register #(.width(12)) MAR (.Q(Address), .clk(CLK_out));  // open: D, en, clr
  Register #(.width(16)) MBR (.Q(MBR_q), .clk(CLK_out));  // open: D, en, clr
  ALU alu_1 (.A(MBR_q), .out_4(alu_1_out_4));  // open: B, sel
  Multiplexer #(.width(16), .enable("false")) multiplexer_1 (
    .in1(alu_1_out_4), .out(multiplexer_1_out));  // open: in0, sel
  Register #(.width(16)) AC (.D(multiplexer_1_out), .Q(AC_q), .clk(CLK_out));  // open: en, clr
  Demultiplexer #(.width(16), .enable("false")) demultiplexer_1 (.in(AC_q));  // open: out0, out1, sel
endmodule
