// Logisim project CTRL unit.circ as structural Verilog: 1 circuit, main circuit main
module main (
  input  [15:0] in_1,
  input  in_2,
  input  in_3,
  output out_4,
  output out_5,
  output out_6,
  output out_7,
  output out_8,
  output out_9,
  output out_10,
  output out_11,
  output out_12,
  output out_13,
  output [11:0] out_14
);

  wire [1:0] counter_1_q;
  wire [3:0] multiplexer_1_out;
  wire [9:9] rom_1_data;
  wire [11:0] PC_q;
  wire [15:0] counter_2_q;

  Counter #(.width(2), .max('h3)) counter_1 (.Q(counter_1_q), .clk(in_3));  // open: load, D, count, carry, clr
  Counter #(.width(16), .max('hffff)) counter_2 (
    .D(in_1), .count(rom_1_data[9]), .Q(counter_2_q), .clk(counter_1_q[1]));  // open: load, carry, clr
  Multiplexer #(.width(4), .enable("false")) multiplexer_1 (
    .in0(4'b0000), .in1(counter_2_q[15:12]), .out(multiplexer_1_out), .sel(counter_1_q[1]));
  Counter #(.width(12), .max('hfff)) PC (.Q(PC_q), .clk(counter_1_q[1]), .clr(in_2));  // open: load, D, count, carry
  Multiplexer #(.width(12), .enable("false")) multiplexer_2 (
    .in0(PC_q), .in1(counter_2_q[11:0]), .out(out_14), .sel(counter_1_q[1]));
  ROM #(.addrWidth(4), .dataWidth(11)) rom_1 (
    .addr(multiplexer_1_out),
    .data({out_13, rom_1_data[9], out_12, out_11, out_10, out_9, out_8, out_7, out_6, out_5, out_4}));  // open: sel
endmodule
