// Logisim project Sterling L 4bit ripple carry adder.circ as structural Verilog: 2 circuits, main circuit adder
module main (
  input  A,
  input  in_2,
  input  B,
  input  Cin,
  output Out,
  output Cout
);

  wire and_1_out, and_2_out, multiplexer_1_out, not_1_out, xor_1_out;

  Multiplexer #(.enable("false")) multiplexer_1 (.in0(A), .in1(not_1_out), .out(multiplexer_1_out), .sel(in_2));
  not not_1 (not_1_out, A);
  xor xor_1 (xor_1_out, multiplexer_1_out, B);
  and and_1 (and_1_out, multiplexer_1_out, B);
  and and_2 (and_2_out, xor_1_out, Cin);
  xor xor_2 (Out, xor_1_out, Cin);
  or or_1 (Cout, and_2_out, and_1_out);
endmodule

module adder (
  input  [3:0] A,
  input  Cin,
  input  in_3,
  input  [3:0] B,
  output [3:0] out_5,
  output [4:0] out_6
);

  wire main_1_cout, main_2_cout, main_3_cout;

  // Probe on B
  // Probe on A
  main main_1 (.A(A[0]), .Out(out_5[0]), .B(B[0]), .Cout(main_1_cout), .Cin(in_3), .in_2(in_3));
  main main_2 (.A(A[1]), .Out(out_5[1]), .B(B[1]), .Cout(main_2_cout), .Cin(main_1_cout), .in_2(in_3));
  main main_3 (.A(A[2]), .Out(out_5[2]), .B(B[2]), .Cout(main_3_cout), .Cin(main_2_cout), .in_2(in_3));
  main main_4 (.A(A[3]), .Out(out_5[3]), .B(B[3]), .Cout(out_6[4]), .Cin(main_3_cout), .in_2(in_3));
  // Probe on out_5
  // Probe on {out_6[4], out_5}

  assign out_6[3:0] = out_5;
endmodule
