// Logisim project Sterling L 8x8 mem.circ as structural Verilog: 1 circuit, main circuit main
module main (
  input  [7:0] Data,
  input  [2:0] Addr,
  output [7:0] Read
);

  wire button_1_out, demultiplexer_1_out0, demultiplexer_1_out1, demultiplexer_1_out2, demultiplexer_1_out3,
       demultiplexer_1_out4, demultiplexer_1_out5, demultiplexer_1_out6, demultiplexer_1_out7;
  wire [7:0] d_ff_57_q, d_ff_58_q, d_ff_59_q, d_ff_60_q, d_ff_61_q, d_ff_62_q, d_ff_63_q, d_ff_64_q,
       demultiplexer_2_out0, demultiplexer_2_out1, demultiplexer_2_out2, demultiplexer_2_out3,
       demultiplexer_2_out4, demultiplexer_2_out5, demultiplexer_2_out6, demultiplexer_2_out7;

  Button button_1 (.out(button_1_out));
  Demultiplexer #(.select(3), .enable("false")) demultiplexer_1 (
    .out0(demultiplexer_1_out0), .out1(demultiplexer_1_out1), .out2(demultiplexer_1_out2),
    .out3(demultiplexer_1_out3), .out4(demultiplexer_1_out4), .out5(demultiplexer_1_out5),
    .out6(demultiplexer_1_out6), .out7(demultiplexer_1_out7), .in(1'b1), .sel(Addr));
  Demultiplexer #(.select(3), .width(8), .enable("false")) demultiplexer_2 (
    .out0(demultiplexer_2_out0), .out1(demultiplexer_2_out1), .out2(demultiplexer_2_out2),
    .out3(demultiplexer_2_out3), .out4(demultiplexer_2_out4), .out5(demultiplexer_2_out5),
    .out6(demultiplexer_2_out6), .out7(demultiplexer_2_out7), .in(Data), .sel(Addr));
  D_Flip_Flop d_ff_1 (
    .clk(button_1_out), .D(demultiplexer_2_out0[7]), .Q(d_ff_57_q[7]), .en(demultiplexer_1_out0));  // open: Qn, preset, reset
  D_Flip_Flop d_ff_2 (
    .clk(button_1_out), .D(demultiplexer_2_out1[7]), .Q(d_ff_58_q[7]), .en(demultiplexer_1_out1));  // open: Qn, preset, reset
  D_Flip_Flop d_ff_3 (
    .clk(button_1_out), .D(demultiplexer_2_out2[7]), .Q(d_ff_59_q[7]), .en(demultiplexer_1_out2));  // open: Qn, preset, reset
  D_Flip_Flop d_ff_4 (
    .clk(button_1_out), .D(demultiplexer_2_out3[7]), .Q(d_ff_60_q[7]), .en(demultiplexer_1_out3));  // open: Qn, preset, reset
  D_Flip_Flop d_ff_5 (
    .clk(button_1_out), .D(demultiplexer_2_out4[7]), .Q(d_ff_61_q[7]), .en(demultiplexer_1_out4));  // open: Qn, preset, reset
  D_Flip_Flop d_ff_6 (
    .clk(button_1_out), .D(demultiplexer_2_out5[7]), .Q(d_ff_62_q[7]), .en(demultiplexer_1_out5));  // open: Qn, preset, reset
  D_Flip_Flop d_ff_7 (
    .clk(button_1_out), .D(demultiplexer_2_out6[7]), .Q(d_ff_63_q[7]), .en(demultiplexer_1_out6));  // open: Qn, preset, reset
  D_Flip_Flop d_ff_8 (
    .clk(button_1_out), .D(demultiplexer_2_out7[7]), .Q(d_ff_64_q[7]), .en(demultiplexer_1_out7));  // open: Qn, preset, reset
  D_Flip_Flop d_ff_9 (
    .clk(button_1_out), .D(demultiplexer_2_out0[6]), .Q(d_ff_57_q[6]), .en(demultiplexer_1_out0));  // open: Qn, preset, reset
  D_Flip_Flop d_ff_10 (
    .clk(button_1_out), .D(demultiplexer_2_out1[6]), .Q(d_ff_58_q[6]), .en(demultiplexer_1_out1));  // open: Qn, preset, reset
  D_Flip_Flop d_ff_11 (
    .clk(button_1_out), .D(demultiplexer_2_out2[6]), .Q(d_ff_59_q[6]), .en(demultiplexer_1_out2));  // open: Qn, preset, reset
  D_Flip_Flop d_ff_12 (
    .clk(button_1_out), .D(demultiplexer_2_out3[6]), .Q(d_ff_60_q[6]), .en(demultiplexer_1_out3));  // open: Qn, preset, reset
  D_Flip_Flop d_ff_13 (
    .clk(button_1_out), .D(demultiplexer_2_out4[6]), .Q(d_ff_61_q[6]), .en(demultiplexer_1_out4));  // open: Qn, preset, reset
  D_Flip_Flop d_ff_14 (
    .clk(button_1_out), .D(demultiplexer_2_out5[6]), .Q(d_ff_62_q[6]), .en(demultiplexer_1_out5));  // open: Qn, preset, reset
  D_Flip_Flop d_ff_15 (
    .clk(button_1_out), .D(demultiplexer_2_out6[6]), .Q(d_ff_63_q[6]), .en(demultiplexer_1_out6));  // open: Qn, preset, reset
  D_Flip_Flop d_ff_16 (
    .clk(button_1_out), .D(demultiplexer_2_out7[6]), .Q(d_ff_64_q[6]), .en(demultiplexer_1_out7));  // open: Qn, preset, reset
  D_Flip_Flop d_ff_17 (
    .clk(button_1_out), .D(demultiplexer_2_out0[5]), .Q(d_ff_57_q[5]), .en(demultiplexer_1_out0));  // open: Qn, preset, reset
  D_Flip_Flop d_ff_18 (
    .clk(button_1_out), .D(demultiplexer_2_out1[5]), .Q(d_ff_58_q[5]), .en(demultiplexer_1_out1));  // open: Qn, preset, reset
  D_Flip_Flop d_ff_19 (
    .clk(button_1_out), .D(demultiplexer_2_out2[5]), .Q(d_ff_59_q[5]), .en(demultiplexer_1_out2));  // open: Qn, preset, reset
  D_Flip_Flop d_ff_20 (
    .clk(button_1_out), .D(demultiplexer_2_out3[5]), .Q(d_ff_60_q[5]), .en(demultiplexer_1_out3));  // open: Qn, preset, reset
  D_Flip_Flop d_ff_21 (
    .clk(button_1_out), .D(demultiplexer_2_out4[5]), .Q(d_ff_61_q[5]), .en(demultiplexer_1_out4));  // open: Qn, preset, reset
  D_Flip_Flop d_ff_22 (
    .clk(button_1_out), .D(demultiplexer_2_out5[5]), .Q(d_ff_62_q[5]), .en(demultiplexer_1_out5));  // open: Qn, preset, reset
  D_Flip_Flop d_ff_23 (
    .clk(button_1_out), .D(demultiplexer_2_out6[5]), .Q(d_ff_63_q[5]), .en(demultiplexer_1_out6));  // open: Qn, preset, reset
  D_Flip_Flop d_ff_24 (
    .clk(button_1_out), .D(demultiplexer_2_out7[5]), .Q(d_ff_64_q[5]), .en(demultiplexer_1_out7));  // open: Qn, preset, reset
  D_Flip_Flop d_ff_25 (
    .clk(button_1_out), .D(demultiplexer_2_out0[4]), .Q(d_ff_57_q[4]), .en(demultiplexer_1_out0));  // open: Qn, preset, reset
  D_Flip_Flop d_ff_26 (
    .clk(button_1_out), .D(demultiplexer_2_out1[4]), .Q(d_ff_58_q[4]), .en(demultiplexer_1_out1));  // open: Qn, preset, reset
  D_Flip_Flop d_ff_27 (
    .clk(button_1_out), .D(demultiplexer_2_out2[4]), .Q(d_ff_59_q[4]), .en(demultiplexer_1_out2));  // open: Qn, preset, reset
  D_Flip_Flop d_ff_28 (
    .clk(button_1_out), .D(demultiplexer_2_out3[4]), .Q(d_ff_60_q[4]), .en(demultiplexer_1_out3));  // open: Qn, preset, reset
  D_Flip_Flop d_ff_29 (
    .clk(button_1_out), .D(demultiplexer_2_out4[4]), .Q(d_ff_61_q[4]), .en(demultiplexer_1_out4));  // open: Qn, preset, reset
  D_Flip_Flop d_ff_30 (
    .clk(button_1_out), .D(demultiplexer_2_out5[4]), .Q(d_ff_62_q[4]), .en(demultiplexer_1_out5));  // open: Qn, preset, reset
  D_Flip_Flop d_ff_31 (
    .clk(button_1_out), .D(demultiplexer_2_out6[4]), .Q(d_ff_63_q[4]), .en(demultiplexer_1_out6));  // open: Qn, preset, reset
  D_Flip_Flop d_ff_32 (
    .clk(button_1_out), .D(demultiplexer_2_out7[4]), .Q(d_ff_64_q[4]), .en(demultiplexer_1_out7));  // open: Qn, preset, reset
  D_Flip_Flop d_ff_33 (
    .clk(button_1_out), .D(demultiplexer_2_out0[3]), .Q(d_ff_57_q[3]), .en(demultiplexer_1_out0));  // open: Qn, preset, reset
  D_Flip_Flop d_ff_34 (
    .clk(button_1_out), .D(demultiplexer_2_out1[3]), .Q(d_ff_58_q[3]), .en(demultiplexer_1_out1));  // open: Qn, preset, reset
  D_Flip_Flop d_ff_35 (
    .clk(button_1_out), .D(demultiplexer_2_out2[3]), .Q(d_ff_59_q[3]), .en(demultiplexer_1_out2));  // open: Qn, preset, reset
  D_Flip_Flop d_ff_36 (
    .clk(button_1_out), .D(demultiplexer_2_out3[3]), .Q(d_ff_60_q[3]), .en(demultiplexer_1_out3));  // open: Qn, preset, reset
  D_Flip_Flop d_ff_37 (
    .clk(button_1_out), .D(demultiplexer_2_out4[3]), .Q(d_ff_61_q[3]), .en(demultiplexer_1_out4));  // open: Qn, preset, reset
  D_Flip_Flop d_ff_38 (
    .clk(button_1_out), .D(demultiplexer_2_out5[3]), .Q(d_ff_62_q[3]), .en(demultiplexer_1_out5));  // open: Qn, preset, reset
  D_Flip_Flop d_ff_39 (
    .clk(button_1_out), .D(demultiplexer_2_out6[3]), .Q(d_ff_63_q[3]), .en(demultiplexer_1_out6));  // open: Qn, preset, reset
  D_Flip_Flop d_ff_40 (
    .clk(button_1_out), .D(demultiplexer_2_out7[3]), .Q(d_ff_64_q[3]), .en(demultiplexer_1_out7));  // open: Qn, preset, reset
  D_Flip_Flop d_ff_41 (
    .clk(button_1_out), .D(demultiplexer_2_out0[2]), .Q(d_ff_57_q[2]), .en(demultiplexer_1_out0));  // open: Qn, preset, reset
  D_Flip_Flop d_ff_42 (
    .clk(button_1_out), .D(demultiplexer_2_out1[2]), .Q(d_ff_58_q[2]), .en(demultiplexer_1_out1));  // open: Qn, preset, reset
  D_Flip_Flop d_ff_43 (
    .clk(button_1_out), .D(demultiplexer_2_out2[2]), .Q(d_ff_59_q[2]), .en(demultiplexer_1_out2));  // open: Qn, preset, reset
  D_Flip_Flop d_ff_44 (
    .clk(button_1_out), .D(demultiplexer_2_out3[2]), .Q(d_ff_60_q[2]), .en(demultiplexer_1_out3));  // open: Qn, preset, reset
  D_Flip_Flop d_ff_45 (
    .clk(button_1_out), .D(demultiplexer_2_out4[2]), .Q(d_ff_61_q[2]), .en(demultiplexer_1_out4));  // open: Qn, preset, reset
  D_Flip_Flop d_ff_46 (
    .clk(button_1_out), .D(demultiplexer_2_out5[2]), .Q(d_ff_62_q[2]), .en(demultiplexer_1_out5));  // open: Qn, preset, reset
  D_Flip_Flop d_ff_47 (
    .clk(button_1_out), .D(demultiplexer_2_out6[2]), .Q(d_ff_63_q[2]), .en(demultiplexer_1_out6));  // open: Qn, preset, reset
  D_Flip_Flop d_ff_48 (
    .clk(button_1_out), .D(demultiplexer_2_out7[2]), .Q(d_ff_64_q[2]), .en(demultiplexer_1_out7));  // open: Qn, preset, reset
  D_Flip_Flop d_ff_49 (
    .clk(button_1_out), .D(demultiplexer_2_out0[1]), .Q(d_ff_57_q[1]), .en(demultiplexer_1_out0));  // open: Qn, preset, reset
  D_Flip_Flop d_ff_50 (
    .clk(button_1_out), .D(demultiplexer_2_out1[1]), .Q(d_ff_58_q[1]), .en(demultiplexer_1_out1));  // open: Qn, preset, reset
  D_Flip_Flop d_ff_51 (
    .clk(button_1_out), .D(demultiplexer_2_out2[1]), .Q(d_ff_59_q[1]), .en(demultiplexer_1_out2));  // open: Qn, preset, reset
  D_Flip_Flop d_ff_52 (
    .clk(button_1_out), .D(demultiplexer_2_out3[1]), .Q(d_ff_60_q[1]), .en(demultiplexer_1_out3));  // open: Qn, preset, reset
  D_Flip_Flop d_ff_53 (
    .clk(button_1_out), .D(demultiplexer_2_out4[1]), .Q(d_ff_61_q[1]), .en(demultiplexer_1_out4));  // open: Qn, preset, reset
  D_Flip_Flop d_ff_54 (
    .clk(button_1_out), .D(demultiplexer_2_out5[1]), .Q(d_ff_62_q[1]), .en(demultiplexer_1_out5));  // open: Qn, preset, reset
  D_Flip_Flop d_ff_55 (
    .clk(button_1_out), .D(demultiplexer_2_out6[1]), .Q(d_ff_63_q[1]), .en(demultiplexer_1_out6));  // open: Qn, preset, reset
  D_Flip_Flop d_ff_56 (
    .clk(button_1_out), .D(demultiplexer_2_out7[1]), .Q(d_ff_64_q[1]), .en(demultiplexer_1_out7));  // open: Qn, preset, reset
  D_Flip_Flop d_ff_57 (
    .clk(button_1_out), .D(demultiplexer_2_out0[0]), .Q(d_ff_57_q[0]), .en(demultiplexer_1_out0));  // open: Qn, preset, reset
  D_Flip_Flop d_ff_58 (
    .clk(button_1_out), .D(demultiplexer_2_out1[0]), .Q(d_ff_58_q[0]), .en(demultiplexer_1_out1));  // open: Qn, preset, reset
  D_Flip_Flop d_ff_59 (
    .clk(button_1_out), .D(demultiplexer_2_out2[0]), .Q(d_ff_59_q[0]), .en(demultiplexer_1_out2));  // open: Qn, preset, reset
  D_Flip_Flop d_ff_60 (
    .clk(button_1_out), .D(demultiplexer_2_out3[0]), .Q(d_ff_60_q[0]), .en(demultiplexer_1_out3));  // open: Qn, preset, reset
  D_Flip_Flop d_ff_61 (
    .clk(button_1_out), .D(demultiplexer_2_out4[0]), .Q(d_ff_61_q[0]), .en(demultiplexer_1_out4));  // open: Qn, preset, reset
  D_Flip_Flop d_ff_62 (
    .clk(button_1_out), .D(demultiplexer_2_out5[0]), .Q(d_ff_62_q[0]), .en(demultiplexer_1_out5));  // open: Qn, preset, reset
  D_Flip_Flop d_ff_63 (
    .clk(button_1_out), .D(demultiplexer_2_out6[0]), .Q(d_ff_63_q[0]), .en(demultiplexer_1_out6));  // open: Qn, preset, reset
  D_Flip_Flop d_ff_64 (
    .clk(button_1_out), .D(demultiplexer_2_out7[0]), .Q(d_ff_64_q[0]), .en(demultiplexer_1_out7));  // open: Qn, preset, reset
  Multiplexer #(.select(3), .width(8), .enable("false")) multiplexer_1 (
    .in0(d_ff_57_q), .in1(d_ff_58_q), .in2(d_ff_59_q), .in3(d_ff_60_q), .in4(d_ff_61_q), .in5(d_ff_62_q),
    .in6(d_ff_63_q), .in7(d_ff_64_q), .out(Read), .sel(Addr));

  // Notes on the sheet:
  //   R/W
  //   Clock
  //   0
  //   1
  //   2
  //   3
  //   4
  //   5
  //   6
  //   7
  //   MSB
  //   This is the 8x8 memory circuit. I basically just widened buses and linked 4 copies of the 4x4 we did in class.
  //   Sterling LaBarbera
  //   3691710
  //   LSB
endmodule
