// Logisim project Sterling L COMPUTER rev3.circ as structural Verilog: 4 circuits, main circuit COMPUTER
module ALU (
  input  [15:0] A,
  input  [15:0] B,
  input  sel,
  output [15:0] out_4
);

  wire [15:0] adder_1_out, subtractor_1_out;

  Adder #(.width(16)) adder_1 (.a(A), .b(B), .out(adder_1_out));  // open: cin, cout
  Subtractor #(.width(16)) subtractor_1 (.a(A), .b(B), .out(subtractor_1_out));  // open: bin, bout
  Multiplexer #(.width(16), .enable("false")) multiplexer_1 (
    .in0(adder_1_out), .in1(subtractor_1_out), .out(out_4), .sel(sel));
endmodule

module CTRL_Unit (
  input  [15:0] Instr,
  input  reset,
  input  clk,
  output Data_Read,
  output MBR_R_W,
  output AC_Data_ALU,
  output AC_R_W,
  output AC_ALU_Out,
  output out_9,
  output MAR_R_W,
  output Load,
  output Store,
  output Halt,
  output [11:0] Address
);

  wire [1:0] counter_1_q;
  wire [3:0] multiplexer_1_out;
  wire [9:9] rom_1_data;
  wire [11:0] PC_q;
  wire [15:0] counter_2_q;

  Counter #(.width(2), .max('h3)) counter_1 (.Q(counter_1_q), .clk(clk));  // open: load, D, count, carry, clr
  Counter #(.width(16), .max('hffff)) counter_2 (
    .D(Instr), .count(rom_1_data[9]), .Q(counter_2_q), .clk(counter_1_q[1]), .clr(reset));  // open: load, carry
  Multiplexer #(.width(4), .enable("false")) multiplexer_1 (
    .in0(4'b0000), .in1(counter_2_q[15:12]), .out(multiplexer_1_out), .sel(counter_1_q[1]));
  Counter #(.width(12), .max('hfff)) PC (.Q(PC_q), .clk(counter_1_q[1]), .clr(reset));  // open: load, D, count, carry
  Multiplexer #(.width(12), .enable("false")) multiplexer_2 (
    .in0(PC_q), .in1(counter_2_q[11:0]), .out(Address), .sel(counter_1_q[1]));
  ROM #(.addrWidth(4), .dataWidth(11)) rom_1 (
    .addr(multiplexer_1_out),
    .data({Halt, rom_1_data[9], Store, Load, MAR_R_W, out_9, AC_ALU_Out, AC_R_W, AC_Data_ALU, MBR_R_W, Data_Read}));  // open: sel

  // Notes on the sheet:
  //   MSB/Opcode
  //   IR R/W
  //   contents of rom_1 (hex, n*v repeats v):
  //   6c1 4cb 550 40c 42c 10*0 400
endmodule

module COMPUTER (
);

  wire and_1_out, clock_1_out, CPU_halt, CPU_load, CPU_store, RESET_out;
  wire [11:0] CPU_address;
  wire [15:0] CPU_data_out, ram_1_data;

  Button RESET (.out(RESET_out));
  RAM #(.addrWidth(12), .dataWidth(16), .bus("separate")) ram_1 (
    .addr(CPU_address), .din(CPU_data_out), .data(ram_1_data), .str(CPU_store), .sel(1'b1), .clk(and_1_out),
    .ld(CPU_load), .clr(RESET_out));
  and and_1 (and_1_out, clock_1_out, CPU_halt);
  Clock clock_1 (.out(clock_1_out));
  CPU CPU (
    .Data_Out(CPU_data_out), .in_1(ram_1_data), .reset(RESET_out), .Address(CPU_address), .Load(CPU_load),
    .Store(CPU_store), .Halt(CPU_halt), .CLK(and_1_out));

  // Notes on the sheet:
  //   Data Read
  //   HALT
  //   Load
  //   Store
  //   Data
  //   Address
endmodule

module CPU (
  input  [15:0] in_1,
  input  reset,
  input  CLK,
  output [15:0] Data_Out,
  output [11:0] Address,
  output Load,
  output Store,
  output Halt
);

  wire ctrl_unit_1_ac_alu_out, ctrl_unit_1_ac_data_alu, ctrl_unit_1_ac_r_w, ctrl_unit_1_data_read,
       ctrl_unit_1_mar_r_w, ctrl_unit_1_mbr_r_w, ctrl_unit_1_out_9;
  wire [11:0] ctrl_unit_1_address;
  wire [15:0] AC_q, alu_1_out_4, controlled_buffer_1_out, demultiplexer_1_out0, MBR_q, multiplexer_1_out;

  CTRL_Unit ctrl_unit_1 (
    .Instr(controlled_buffer_1_out), .reset(reset), .Data_Read(ctrl_unit_1_data_read),
    .MBR_R_W(ctrl_unit_1_mbr_r_w), .AC_Data_ALU(ctrl_unit_1_ac_data_alu), .AC_R_W(ctrl_unit_1_ac_r_w),
    .AC_ALU_Out(ctrl_unit_1_ac_alu_out), .out_9(ctrl_unit_1_out_9), .MAR_R_W(ctrl_unit_1_mar_r_w),
    .Load(Load), .Store(Store), .Halt(Halt), .Address(ctrl_unit_1_address), .clk(CLK));
  assign controlled_buffer_1_out = ctrl_unit_1_data_read ? in_1 : 16'bz;  // Controlled_Buffer controlled_buffer_1
  Register #(.width(12)) MAR (.D(ctrl_unit_1_address), .en(ctrl_unit_1_mar_r_w), .Q(Address), .clk(CLK));  // open: clr
  Register #(.width(16)) MBR (
    .D(controlled_buffer_1_out), .en(ctrl_unit_1_mbr_r_w), .Q(MBR_q), .clk(CLK));  // open: clr
  ALU alu_1 (.A(demultiplexer_1_out0), .B(MBR_q), .out_4(alu_1_out_4), .sel(ctrl_unit_1_out_9));
  Multiplexer #(.width(16), .enable("false")) multiplexer_1 (
    .in0(controlled_buffer_1_out), .in1(alu_1_out_4), .out(multiplexer_1_out), .sel(ctrl_unit_1_ac_data_alu));
  Register #(.width(16)) AC (.D(multiplexer_1_out), .en(ctrl_unit_1_ac_r_w), .Q(AC_q), .clk(CLK));  // open: clr
  Demultiplexer #(.width(16), .enable("false")) demultiplexer_1 (
    .out0(demultiplexer_1_out0), .out1(Data_Out), .in(AC_q), .sel(ctrl_unit_1_ac_alu_out));
endmodule
